# Fritzing sketch bme280-ads1115-ldr-humidity-wiring (saved by Fritzing 1.0.6)
breadboards: 1

parts:
  A1 = Esp32-c3 super mini
  A2 = GY-BMP280 Breakout
  GY-ADS1 = GY-ADS1115 16Bit I2C ADC [part_number="Adafruit #1085"]
  R1 = Photocell (LDR) [power=0.25W dark_resistance_@0.01lx=300kΩ light_resistance_@100lx=400Ω luminance=10lx package=THT]
  R2 = Resistor [tolerance=±5% power=0.25W resistance=1k package=THT]

nets:
  N1: A1.Pin_4, A2.Pin_4, GY-ADS1.SDA
  N2: A1.Pin_5, A2.Pin_3, GY-ADS1.SCL
  N3: A1.Pin_14, A2.Pin_1, A2.Pin_5, GY-ADS1.VDD, R2.Pin_1
  N4: A1.Pin_15, A2.Pin_2, A2.Pin_6, GY-ADS1.ADDR, GY-ADS1.GND, R1.pin_0
  N5: GY-ADS1.AIN0, R1.pin_1, R2.Pin_0

custom parts:
  Esp32-c3 super mini: ESP32-C3 Development Board ESP32 SuperMini Development Board ESP32 Development Board WiFi Bluetooth.
  GY-ADS1115 16Bit I2C ADC: For microcontrollers without an analog-to-digital converter or when you want a higher-precision ADC, the ADS1115 provides 16-bit precision at 860 samples/second over I2C. The chip can be configured as 4 single-ended input channels, or two differential channels. As a nice bonus, it even includes a programmable gain amplifier, up to x16, to help boost up smaller single/differential signals to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
